// Logisim project ISA.circ as structural Verilog: 6 circuits, main circuit main
module main (
);

  ULA ula_1 ();  // open: seletor, A, B, Resultado
endmodule

module ULA (
  input  [2:0] seletor,
  input  [11:0] A,
  input  [11:0] B,
  output [11:0] Resultado
);

  wire [11:0] adder_1_out, and_1_out, not_1_out, or_1_out, subtractor_1_out;

  Adder #(.width(12)) adder_1 (.a(A), .b(B), .out(adder_1_out));  // open: cin, cout
  Subtractor #(.width(12)) subtractor_1 (.a(A), .b(B), .out(subtractor_1_out));  // open: bin, bout
  assign not_1_out = ~A;  // NOT_Gate not_1, 12 bits wide
  assign and_1_out = A & B;  // AND_Gate and_1, 12 bits wide
  assign or_1_out = A | B;  // OR_Gate or_1, 12 bits wide
  Multiplexer #(.select(3), .width(12)) multiplexer_1 (
    .in0(adder_1_out), .in1(subtractor_1_out), .in2(and_1_out), .in3(or_1_out), .in4(not_1_out),
    .out(Resultado), .sel(seletor));  // open: in5, in6, in7
endmodule

module BD (
  input  [11:0] WRITEDATA,
  input  [1:0] RS1,
  input  [1:0] RS2,
  input  regwrite,
  input  [1:0] RD,
  output [11:0] ReadData1,
  output [11:0] ReadData2
);

  wire R0, R1, R2, R3;
  wire [11:0] S0, S1, S2, S3;

  Register #(.width(12)) u_R0 (.D(WRITEDATA), .en(R0), .Q(S0));  // open: clk, clr
  Register #(.width(12)) u_R1 (.D(WRITEDATA), .en(R1), .Q(S1));  // open: clk, clr
  Register #(.width(12)) u_R2 (.D(WRITEDATA), .en(R2), .Q(S2));  // open: clk, clr
  Register #(.width(12)) u_R3 (.D(WRITEDATA), .en(R3), .Q(S3));  // open: clk, clr
  Demultiplexer #(.select(2)) demultiplexer_1 (.out0(R0), .out1(R1), .out2(R2), .out3(R3), .in(regwrite), .sel(RD));
  Multiplexer #(.select(2), .width(12)) multiplexer_1 (
    .in0(S0), .in1(S1), .in2(S2), .in3(S3), .out(ReadData1), .sel(RS1));
  Multiplexer #(.select(2), .width(12)) multiplexer_2 (
    .in0(S0), .in1(S1), .in2(S2), .in3(S3), .out(ReadData2), .sel(RS2));
endmodule

module PC (
  input  RESET,
  output [9:0] Q
);

  wire clock_1_out;
  wire [9:0] adder_1_out;

  Clock clock_1 (.out(clock_1_out));
  Register #(.width(10)) register_1 (.D(adder_1_out), .en(1'b1), .clk(clock_1_out), .Q(Q), .clr(RESET));
  Adder #(.width(10)) adder_1 (.a(Q), .b(10'h1), .out(adder_1_out));  // open: cin, cout
endmodule

module MI (
);

  wire clock_1_out;
  wire [9:0] pc_1_q;
  wire [11:0] bd_1_readdata1, bd_1_readdata2, ula_1_resultado;
  wire [11:2] ram_1_dout;

  Clock clock_1 (.out(clock_1_out));
  RAM #(.addrWidth(10), .dataWidth(12)) ram_1 (
    .addr(pc_1_q), .we(1'b0), .oe(1'b1), .clk(clock_1_out), .dout({ram_1_dout, ram_1_dout[3:2]}));  // open: din
  PC pc_1 (.Q(pc_1_q));  // open: RESET
  BD bd_1 (
    .WRITEDATA(ula_1_resultado), .RS1(ram_1_dout[5:4]), .RS2(ram_1_dout[3:2]), .regwrite(1'b1),
    .RD(ram_1_dout[7:6]), .ReadData1(bd_1_readdata1), .ReadData2(bd_1_readdata2));
  ULA ula_1 (.A(bd_1_readdata1), .B(bd_1_readdata2), .Resultado(ula_1_resultado));  // open: seletor
endmodule

module UC (
  input  [3:0] OPCODE,
  input  [1:0] FUNC,
  output RegWrite,
  output ALUOp
);
endmodule
